// Logisim project Berk-Planar.circ as structural Verilog: 1 circuit, main circuit main
module main (
);

  wire and_1_out, and_2_out, and_3_out, and_4_out, and_5_out, and_6_out, and_7_out, and_8_out, and_9_out,
       and_10_out, and_11_out, button_1_out, clock_1_out, comparator_1_eq, comparator_1_lt, d_ff_1_q,
       d_ff_2_q, d_ff_3_q, d_ff_4_q, d_ff_5_q, d_ff_6_q, d_ff_7_q, d_ff_8_q, decoder_1_out0, decoder_1_out1,
       decoder_1_out3, demultiplexer_1_out0, demultiplexer_1_out1, demultiplexer_1_out2,
       demultiplexer_1_out3, demultiplexer_1_out4, demultiplexer_1_out5, demultiplexer_1_out6,
       demultiplexer_1_out7, demultiplexer_2_out0, demultiplexer_2_out1, demultiplexer_2_out2,
       demultiplexer_2_out3, demultiplexer_2_out4, demultiplexer_2_out5, demultiplexer_2_out6,
       demultiplexer_2_out7, multiplexer_16_out, multiplexer_17_out, multiplexer_20_out, nand_1_out,
       nand_2_out, not_1_out, not_2_out, not_3_out, or_1_out, or_2_out, or_3_out, or_5_out, or_6_out,
       RESET_out, START_STOP_out, t_ff_1_q, xnor_1_out, xor_1_out, xor_2_out;
  wire [0:0] multiplexer_7_out, multiplexer_8_out, multiplexer_15_out;
  wire [1:0] controlled_inverter_1_out, counter_1_q;
  wire [2:0] multiplexer_6_out, pull_resistor_3_node, register_2_q, register_2_q_2, register_2_q_3;
  wire [3:0] multiplexer_5_out, subtractor_1_out;
  wire [5:5] or_4_out;
  wire [6:0] adder_3_out, multiplexer_12_out, multiplexer_13_out, pull_resistor_2_node;
  wire [11:0] _0_q, _1_q, _2_q, _3_q, _4_q, _5_q, _6_q, _7_q, adder_1_out, adder_2_out, adder_4_out,
       adder_5_out, divider_1_out, divider_1_rem, divider_2_out, divider_2_rem, divider_3_out, divider_3_rem,
       divider_4_out, divider_4_rem, divider_5_out, divider_5_rem, divider_6_out, divider_6_rem,
       divider_7_out, divider_7_rem, divider_8_out, divider_8_rem, multiplexer_1_out, multiplexer_2_out,
       multiplexer_3_out, multiplexer_4_out, multiplexer_9_out, multiplexer_10_out, multiplexer_11_out,
       multiplexer_14_out, multiplexer_18_out, multiplexer_19_out, multiplexer_21_out, multiplexer_22_out,
       multiplexer_23_out, multiplexer_24_out, multiplexer_25_out, multiplexer_26_out, multiplier_1_out,
       negator_1_out, negator_2_out, negator_3_out, negator_4_out, ram_1_data, register_1_q,
       subtractor_2_out, subtractor_3_out;
  wire [11:9] register_2_q_4;

  Clock clock_1 (.out(clock_1_out));
  not not_1 (not_1_out, clock_1_out);
  Button START_STOP (.out(START_STOP_out));
  Button RESET (.out(RESET_out));
  Button button_1 (.out(button_1_out));
  or or_1 (or_1_out, button_1_out, and_1_out);
  xnor xnor_1 (xnor_1_out, clock_1_out, not_1_out);
  T_Flip_Flop t_ff_1 (.clk(START_STOP_out), .T(1'b1), .Q(t_ff_1_q), .reset(RESET_out));  // open: Qn, preset, en
  Counter #(.width(2), .max('h3), .ongoal("load")) counter_1 (
    .count(1'b1), .Q(counter_1_q), .clk(or_1_out), .clr(RESET_out));  // open: load, D, carry
  Decoder #(.select(2), .disabled(0), .enable("false")) decoder_1 (
    .out0(decoder_1_out0), .out1(decoder_1_out1), .out3(decoder_1_out3), .sel(counter_1_q));  // open: out2
  and and_1 (and_1_out, xnor_1_out, t_ff_1_q);
  Negator #(.width(12)) negator_1 (.in(multiplexer_18_out), .out(negator_1_out));
  Multiplexer #(.width(12), .disabled(0), .enable("false")) multiplexer_1 (
    .in0(multiplexer_18_out), .in1(negator_1_out), .out(multiplexer_1_out), .sel(multiplexer_18_out[11]));
  Adder #(.width(12)) adder_1 (.a(adder_2_out), .b({12{1'b0}}), .out(adder_1_out), .cin(1'b1));  // open: cout
  Divider #(.width(12)) divider_1 (
    .a(multiplexer_1_out), .b(12'ha), .out(divider_1_out), .rem(divider_1_rem));  // open: upper
  Divider #(.width(12)) divider_2 (
    .a(divider_1_out), .b(12'ha), .out(divider_2_out), .rem(divider_2_rem));  // open: upper
  Multiplexer #(.width(12), .enable("false")) multiplexer_2 (
    .in0(12'hfd0), .in1(12'hffd), .out(multiplexer_2_out), .sel(multiplexer_18_out[11]));
  Divider #(.width(12)) divider_3 (
    .a(multiplexer_18_out), .b(12'ha), .out(divider_3_out), .rem(divider_3_rem));  // open: upper
  Divider #(.width(12)) divider_4 (
    .a(divider_3_out), .b(12'ha), .out(divider_4_out), .rem(divider_4_rem));  // open: upper
  Adder #(.width(12)) adder_2 (.a(register_1_q), .b({12{1'b0}}), .out(adder_2_out), .cin(1'b1));  // open: cout
  Multiplexer #(.select(3), .width(12), .disabled(0), .enable("false")) multiplexer_3 (
    .in0(ram_1_data), .in1(ram_1_data), .in2(adder_1_out), .in3(ram_1_data), .in4(multiplexer_18_out),
    .in5(adder_2_out), .in6(multiplexer_18_out), .in7(multiplexer_18_out), .out(multiplexer_3_out),
    .sel({register_2_q[1:0], multiplexer_15_out[0]}));
  Divider #(.width(12)) divider_5 (
    .a(divider_2_out), .b(12'ha), .out(divider_5_out), .rem(divider_5_rem));  // open: upper
  Divider #(.width(12)) divider_6 (
    .a(divider_4_out), .b(12'ha), .out(divider_6_out), .rem(divider_6_rem));  // open: upper
  and and_2 (and_2_out, ~register_2_q_4[9], register_2_q_4[10], ~register_2_q_4[11]);  // AND_Gate
  assign controlled_inverter_1_out = and_2_out ? ~{register_2_q[0], register_2_q[2]} : 2'bz;  // Controlled_Inverter controlled_inverter_1
  Pull_Resistor pull_resistor_1 (.node(controlled_inverter_1_out));
  Multiplexer #(.select(2), .width(12), .disabled(0), .enable("false")) multiplexer_4 (
    .in0(adder_2_out), .in1(multiplexer_3_out), .in2(adder_1_out), .in3(multiplexer_3_out),
    .out(multiplexer_4_out), .sel(controlled_inverter_1_out));
  and and_3 (and_3_out, ~register_2_q_4[11], register_2_q_4[10], register_2_q_4[9]);  // AND_Gate
  Multiplexer #(.select(2), .width(4), .disabled(0), .enable("false")) multiplexer_5 (
    .in0(multiplexer_18_out[11:8]), .in1(multiplexer_18_out[7:4]), .in2(multiplexer_18_out[3:0]),
    .in3(4'b0000), .out(multiplexer_5_out), .sel(register_2_q_2[1:0]));
  Multiplexer #(.select(2), .width(3), .disabled(0), .enable("false")) multiplexer_6 (
    .in0(multiplexer_18_out[11:9]), .in1(multiplexer_18_out[8:6]), .in2(multiplexer_18_out[5:3]),
    .in3(multiplexer_18_out[2:0]), .out(multiplexer_6_out), .sel(register_2_q_2[1:0]));
  Multiplexer #(.select(3), .disabled(0), .enable("false")) multiplexer_7 (
    .in0(multiplexer_18_out[7]), .in1(multiplexer_18_out[6]), .in2(multiplexer_18_out[5]),
    .in3(multiplexer_18_out[4]), .in4(multiplexer_18_out[3]), .in5(multiplexer_18_out[2]),
    .in6(multiplexer_18_out[1]), .in7(multiplexer_18_out[0]), .out(multiplexer_7_out[0]), .sel(register_2_q_2));
  Multiplexer #(.select(2), .disabled(0), .enable("false")) multiplexer_8 (
    .in0(multiplexer_18_out[11]), .in1(multiplexer_18_out[10]), .in2(multiplexer_18_out[9]),
    .in3(multiplexer_18_out[8]), .out(multiplexer_8_out[0]), .sel(register_2_q_2[1:0]));
  Multiplexer #(.select(3), .width(12), .disabled(0), .enable("false")) multiplexer_9 (
    .in0(multiplexer_2_out), .in1(divider_5_out), .in2(divider_5_rem), .in3(divider_2_rem),
    .in4(divider_1_rem), .in5({12{1'b0}}), .in6({12{1'b0}}), .in7({12{1'b0}}), .out(multiplexer_9_out),
    .sel(register_2_q_2));
  and and_4 (and_4_out, register_2_q_2[0], register_2_q_2[1]);
  Multiplexer #(.select(2), .width(12), .disabled(0), .enable("false")) multiplexer_10 (
    .in0(divider_6_out), .in1(divider_6_rem), .in2(divider_4_rem), .in3(divider_3_rem),
    .out(multiplexer_10_out), .sel(register_2_q_2[1:0]));
  Register #(.width(12)) register_1 (
    .D(multiplexer_4_out), .Q(register_1_q), .clk(decoder_1_out0), .clr(RESET_out));  // open: en
  or or_2 (or_2_out, multiplexer_5_out[2], multiplexer_5_out[1]);
  Subtractor #(.width(4)) subtractor_1 (.a(multiplexer_5_out), .b(4'b1001), .out(subtractor_1_out));  // open: bin, bout
  or or_3 (or_3_out, register_2_q_2[2], multiplexer_9_out[0], multiplexer_9_out[1], multiplexer_9_out[2], multiplexer_9_out[3]);
  Adder #(.width(7)) adder_3 (.a(multiplexer_9_out[6:0]), .b(7'b0110000), .out(adder_3_out));  // open: cin, cout
  or or_4 (or_4_out[5], and_4_out, multiplexer_10_out[0], multiplexer_10_out[1], multiplexer_10_out[2], multiplexer_10_out[3]);
  Multiplexer #(.select(2), .width(12), .disabled(0), .enable("false")) multiplexer_11 (
    .in0(register_1_q), .in1(register_1_q), .in2(adder_2_out), .in3(multiplexer_18_out),
    .out(multiplexer_11_out), .sel({counter_1_q[1], register_2_q[0]}));
  and and_5 (and_5_out, multiplexer_5_out[3], or_2_out);
  Multiplexer #(.width(7), .disabled(0), .enable("false")) multiplexer_12 (
    .in0({3'b011, multiplexer_5_out}), .in1({3'b110, subtractor_1_out}), .out(multiplexer_12_out),
    .sel(and_5_out));
  Pull_Resistor pull_resistor_2 (.node(pull_resistor_2_node));
  assign pull_resistor_2_node = or_3_out ? adder_3_out : 7'bz;  // Controlled_Buffer controlled_buffer_1
  Multiplexer #(.select(3), .width(7), .disabled(0), .enable("false")) multiplexer_13 (
    .in0({register_2_q[0], register_2_q_3, register_2_q_2}),
    .in1({register_2_q[0], register_2_q_3, register_2_q_2}), .in2(multiplexer_12_out),
    .in3({4'b0011, multiplexer_6_out}), .in4({6'b011000, multiplexer_7_out[0]}),
    .in5({6'b011000, multiplexer_8_out[0]}), .in6(pull_resistor_2_node),
    .in7({1'b0, {2{or_4_out[5]}}, multiplexer_10_out[3:0]}), .out(multiplexer_13_out), .sel(register_2_q));
  TTY #(.rows(12), .cols(40)) tty_1 (.data(multiplexer_13_out), .clk(decoder_1_out3), .we(and_3_out), .clr(RESET_out));
  RAM #(.addrWidth(12), .dataWidth(12), .bus("separate")) ram_1 (
    .addr(multiplexer_11_out), .din(multiplexer_19_out), .data(ram_1_data), .str(and_6_out), .sel(1'b1),
    .clk(decoder_1_out3), .ld(1'b1), .clr(1'b0));
  and and_6 (and_6_out, register_2_q[1], register_2_q[2], ~register_2_q_4[9], register_2_q_4[10], ~register_2_q_4[11]);  // AND_Gate
  Register #(.width(12)) register_2 (
    .D(ram_1_data), .Q({register_2_q_4, register_2_q, register_2_q_3, register_2_q_2}), .clk(decoder_1_out1),
    .clr(RESET_out));  // open: en
  and and_7 (and_7_out, ~register_2_q_4[11], ~register_2_q_4[10], ~register_2_q_4[9]);  // AND_Gate
  and and_8 (and_8_out, ~register_2_q_4[11], ~register_2_q_4[10], register_2_q_4[9]);  // AND_Gate
  or or_5 (or_5_out, and_7_out, and_9_out);
  and and_9 (and_9_out, ~register_2_q_4[11], register_2_q_4[10], ~register_2_q_4[9], register_2_q[2], ~register_2_q[1]);  // AND_Gate
  Multiplexer #(.width(12), .disabled(0), .enable("false")) multiplexer_14 (
    .in0(multiplexer_26_out), .in1(ram_1_data), .out(multiplexer_14_out), .sel(register_2_q_4[10]));
  nand nand_1 (nand_1_out, register_2_q[2], nand_2_out);
  nand nand_2 (nand_2_out, register_2_q[1], register_2_q[0]);
  Pull_Resistor pull_resistor_3 (.node(pull_resistor_3_node));
  Demultiplexer #(.select(3), .disabled(0), .enable("false")) demultiplexer_1 (
    .out0(demultiplexer_1_out0), .out1(demultiplexer_1_out1), .out2(demultiplexer_1_out2),
    .out3(demultiplexer_1_out3), .out4(demultiplexer_1_out4), .out5(demultiplexer_1_out5),
    .out6(demultiplexer_1_out6), .out7(demultiplexer_1_out7), .in(and_10_out), .sel(pull_resistor_3_node));
  and and_10 (and_10_out, decoder_1_out3, and_8_out);
  assign pull_resistor_3_node = nand_1_out ? register_2_q_2 : 3'bz;  // Controlled_Buffer controlled_buffer_2
  Demultiplexer #(.select(3), .enable("false")) demultiplexer_2 (
    .out0(demultiplexer_2_out0), .out1(demultiplexer_2_out1), .out2(demultiplexer_2_out2),
    .out3(demultiplexer_2_out3), .out4(demultiplexer_2_out4), .out5(demultiplexer_2_out5),
    .out6(demultiplexer_2_out6), .out7(demultiplexer_2_out7), .in(or_5_out), .sel(register_2_q_2));
  Register #(.width(12)) _7 (
    .D(multiplexer_14_out), .en(demultiplexer_2_out7), .Q(_7_q), .clk(decoder_1_out3), .clr(RESET_out));
  Register #(.width(12)) _6 (
    .D(multiplexer_14_out), .en(demultiplexer_2_out6), .Q(_6_q), .clk(decoder_1_out3), .clr(RESET_out));
  D_Flip_Flop d_ff_1 (
    .clk(demultiplexer_1_out0), .D(multiplexer_20_out), .Q(d_ff_1_q), .reset(RESET_out));  // open: Qn, preset, en
  D_Flip_Flop d_ff_2 (
    .clk(demultiplexer_1_out1), .D(multiplexer_20_out), .Q(d_ff_2_q), .reset(RESET_out));  // open: Qn, preset, en
  D_Flip_Flop d_ff_3 (
    .clk(demultiplexer_1_out2), .D(multiplexer_20_out), .Q(d_ff_3_q), .reset(RESET_out));  // open: Qn, preset, en
  D_Flip_Flop d_ff_4 (
    .clk(demultiplexer_1_out3), .D(multiplexer_20_out), .Q(d_ff_4_q), .reset(RESET_out));  // open: Qn, preset, en
  D_Flip_Flop d_ff_5 (
    .clk(demultiplexer_1_out4), .D(multiplexer_20_out), .Q(d_ff_5_q), .reset(RESET_out));  // open: Qn, preset, en
  D_Flip_Flop d_ff_6 (
    .clk(demultiplexer_1_out5), .D(multiplexer_20_out), .Q(d_ff_6_q), .reset(RESET_out));  // open: Qn, preset, en
  D_Flip_Flop d_ff_7 (
    .clk(demultiplexer_1_out6), .D(multiplexer_20_out), .Q(d_ff_7_q), .reset(RESET_out));  // open: Qn, preset, en
  D_Flip_Flop d_ff_8 (
    .clk(demultiplexer_1_out7), .D(multiplexer_20_out), .Q(d_ff_8_q), .reset(RESET_out));  // open: Qn, preset, en
  Register #(.width(12)) _5 (
    .D(multiplexer_14_out), .en(demultiplexer_2_out5), .Q(_5_q), .clk(decoder_1_out3), .clr(RESET_out));
  Register #(.width(12)) _3 (
    .D(multiplexer_14_out), .en(demultiplexer_2_out3), .Q(_3_q), .clk(decoder_1_out3), .clr(RESET_out));
  Register #(.width(12)) _4 (
    .D(multiplexer_14_out), .en(demultiplexer_2_out4), .Q(_4_q), .clk(decoder_1_out3), .clr(RESET_out));
  Multiplexer #(.select(3), .disabled(0), .enable("false")) multiplexer_15 (
    .in0(d_ff_1_q), .in1(d_ff_2_q), .in2(d_ff_3_q), .in3(d_ff_4_q), .in4(d_ff_5_q), .in5(d_ff_6_q),
    .in6(d_ff_7_q), .in7(d_ff_8_q), .out(multiplexer_15_out[0]), .sel(register_2_q_2));
  Multiplexer #(.select(3), .disabled(0), .enable("false")) multiplexer_16 (
    .in0(d_ff_1_q), .in1(d_ff_2_q), .in2(d_ff_3_q), .in3(d_ff_4_q), .in4(d_ff_5_q), .in5(d_ff_6_q),
    .in6(d_ff_7_q), .in7(d_ff_8_q), .out(multiplexer_16_out), .sel(register_2_q_3));
  Register #(.width(12)) _2 (
    .D(multiplexer_14_out), .en(demultiplexer_2_out2), .Q(_2_q), .clk(decoder_1_out3), .clr(RESET_out));
  not not_2 (not_2_out, multiplexer_15_out[0]);
  and and_11 (and_11_out, multiplexer_16_out, multiplexer_15_out[0]);
  or or_6 (or_6_out, multiplexer_16_out, multiplexer_15_out[0]);
  Register #(.width(12)) _1 (
    .D(multiplexer_14_out), .en(demultiplexer_2_out1), .Q(_1_q), .clk(decoder_1_out3), .clr(RESET_out));
  Multiplexer #(.select(2), .disabled(0), .enable("false")) multiplexer_17 (
    .in0(multiplexer_15_out[0]), .in1(1'b0), .in2(1'b1), .in3(not_2_out), .out(multiplexer_17_out),
    .sel(register_2_q_3[2:1]));
  xor xor_1 (xor_1_out, multiplexer_16_out, multiplexer_15_out[0]);
  Register #(.width(12)) _0 (
    .D(multiplexer_14_out), .en(demultiplexer_2_out0), .Q(_0_q), .clk(decoder_1_out3), .clr(RESET_out));
  Subtractor #(.width(12)) subtractor_2 (
    .a(multiplexer_19_out), .b(multiplexer_18_out), .out(subtractor_2_out));  // open: bin, bout
  Comparator #(.width(12), .mode("unsigned")) comparator_1 (
    .a(multiplexer_19_out), .b(multiplexer_18_out), .eq(comparator_1_eq), .lt(comparator_1_lt));  // open: gt
  Multiplexer #(.select(3), .width(12), .disabled(0), .enable("false")) multiplexer_18 (
    .in0(_0_q), .in1(_1_q), .in2(_2_q), .in3(_3_q), .in4(_4_q), .in5(_5_q), .in6(_6_q), .in7(_7_q),
    .out(multiplexer_18_out), .sel(register_2_q_3));
  Multiplexer #(.select(3), .width(12), .disabled(0), .enable("false")) multiplexer_19 (
    .in0(_0_q), .in1(_1_q), .in2(_2_q), .in3(_3_q), .in4(_4_q), .in5(_5_q), .in6(_6_q), .in7(_7_q),
    .out(multiplexer_19_out), .sel(register_2_q_2));
  Multiplexer #(.select(3), .disabled(0), .enable("false")) multiplexer_20 (
    .in0(multiplexer_17_out), .in1(and_11_out), .in2(or_6_out), .in3(xor_1_out), .in4(subtractor_2_out[11]),
    .in5(comparator_1_eq), .in6(comparator_1_lt), .in7(multiplexer_16_out), .out(multiplexer_20_out),
    .sel(register_2_q));
  Negator #(.width(12)) negator_2 (.in(multiplexer_19_out), .out(negator_2_out));
  Multiplexer #(.width(12), .disabled(0), .enable("false")) multiplexer_21 (
    .in0(negator_2_out), .in1(multiplexer_19_out), .out(multiplexer_21_out), .sel(negator_2_out[11]));
  Adder #(.width(12)) adder_4 (.a(multiplexer_19_out), .b({12{1'b0}}), .out(adder_4_out), .cin(1'b1));  // open: cout
  Adder #(.width(12)) adder_5 (.a(multiplexer_18_out), .b(multiplexer_19_out), .out(adder_5_out));  // open: cin, cout
  Multiplier #(.width(12)) multiplier_1 (
    .a(multiplexer_18_out), .b(multiplexer_19_out), .out(multiplier_1_out));  // open: cin, cout
  Negator #(.width(12)) negator_3 (.in(multiplexer_18_out), .out(negator_3_out));
  Multiplexer #(.width(12), .disabled(0), .enable("false")) multiplexer_22 (
    .in0(negator_3_out), .in1(multiplexer_18_out), .out(multiplexer_22_out), .sel(negator_3_out[11]));
  Divider #(.width(12)) divider_7 (
    .a(multiplexer_18_out), .b(multiplexer_19_out), .out(divider_7_out), .rem(divider_7_rem));  // open: upper
  Multiplexer #(.select(2), .width(12), .disabled(0), .enable("false")) multiplexer_23 (
    .in0(negator_2_out), .in1(multiplexer_21_out), .in2(adder_4_out), .in3({12{1'b0}}),
    .out(multiplexer_23_out), .sel(register_2_q_3[2:1]));
  Multiplexer #(.width(12), .disabled(0), .enable("false")) multiplexer_24 (
    .in0(negator_4_out), .in1(divider_8_out), .out(multiplexer_24_out), .sel(xor_2_out));
  xor xor_2 (xor_2_out, negator_2_out[11], negator_3_out[11]);
  Negator #(.width(12)) negator_4 (.in(divider_8_out), .out(negator_4_out));
  Divider #(.width(12)) divider_8 (
    .a(multiplexer_22_out), .b(multiplexer_21_out), .out(divider_8_out), .rem(divider_8_rem));  // open: upper
  not not_3 (not_3_out, negator_3_out[11]);
  Multiplexer #(.width(12), .disabled(0), .enable("false")) multiplexer_25 (
    .in0(divider_8_rem), .in1(subtractor_3_out), .out(multiplexer_25_out), .sel(not_3_out));
  Subtractor #(.width(12)) subtractor_3 (
    .a(multiplexer_21_out), .b(divider_8_rem), .out(subtractor_3_out));  // open: bin, bout
  Multiplexer #(.select(3), .width(12), .disabled(0), .enable("false")) multiplexer_26 (
    .in0(multiplexer_23_out), .in1(adder_5_out), .in2(multiplier_1_out), .in3(multiplexer_24_out),
    .in4(multiplexer_25_out), .in5(divider_7_out), .in6(divider_7_rem), .in7(multiplexer_18_out),
    .out(multiplexer_26_out), .sel(register_2_q));

  // Notes on the sheet:
  //   Created and designed by Reuben French
  //   Berk
  //   12 bit computer
endmodule
